# Fritzing sketch capacitive_touch_servo (saved by Fritzing 0.9.5d)

parts:
  A1 = Arduino UNO R4 WiFi
  J1 = Basic Servo

nets:
  N1: A1.Pin_8, A1.Pin_27, J1.vcc
  N2: A1.Pin_9, A1.Pin_30, J1.gnd
  N3: A1.Pin_45, J1.pulse

custom parts:
  Arduino UNO R4 WiFi: The Arduino UNO R4 WiFi merges the RA4M1 microprocessor from Renesas with the ESP32-S3 from Espressif, creating an all-in-one tool for makers with enhanced processing power and a diverse array of new peripherals.
